# Fritzing sketch drawing (saved by Fritzing 0.9.4)

parts:
  Part1 = Arduino Pro Mini v13
  RS485_module1 = RS485 Module (MAX3485)
  LCD2004-I2C1 = LCD2004-I2C
  R1 = Rotary Potentiometer (Small) [maximum_resistance=100kΩ package=THT]
  RE1 = KY-040 Rotary encoder [package=THT]
  Power_plug1 = Power plug
  J1 = screw terminal, 4 pins

nets:
  VCC: Part1.VCC, LCD2004-I2C1.VCC, R1.leg2, RE1.Vcc
  VCC_2: Part1.RAW, RS485_module1.VCC, Power_plug1.VCC
  GND: Part1.GND, RS485_module1.GND, LCD2004-I2C1.GND, R1.leg1, RE1.GND, Power_plug1.GND
  N1: Part1.A0, R1.wiper
  N2: Part1.D7, RS485_module1.RE, RS485_module1.DE
  N3: Part1.D6_PWM, RE1.CLK
  N4: Part1.D5_PWM, RE1.DT
  N5: Part1.D4, RE1.SW
  N6: Part1.D3_PWM, LCD2004-I2C1.SCL
  N7: Part1.D2, LCD2004-I2C1.SDA
  N8: Part1.D1/RX, RS485_module1.RO
  N9: Part1.D0/TX, RS485_module1.DI
  N10: RS485_module1.A, J1.pin2, J1.pin4
  N11: RS485_module1.B, J1.pin1, J1.pin3

notes:
  R- R+ S- S+

custom parts:
  RS485 Module (MAX3485): Commercially available RS485 to RS232 TTL Module
  LCD2004-I2C: A standard character display with 4x20 characters. Comes in many colors with LCM2004 IIC attached.
  KY-040 Rotary encoder: KY-040 Rotary Encoder with switch on breakout borad from AZ Delivery
